# Fritzing sketch accel_on_lcd (saved by Fritzing 0.9.3b)

parts:
  Part1 = Intel Edison Arduinobreakout  # not connected
  Part2 = Base Shield V2
  Grove1 = Grove 3 Axis Digital Accelerometer 16g
  Grove3 = Grove OLED 128x96

nets:
  N1: Part2.pin_124, Grove3.GND
  N2: Part2.pin_125, Grove3.VCC
  N3: Part2.pin_126, Grove3.SDA
  N4: Part2.pin_127, Grove3.SCL
  N5: Part2.pin_136, Grove1.GND
  N6: Part2.pin_137, Grove1.VCC
  N7: Part2.pin_138, Grove1.SDA
  N8: Part2.pin_139, Grove1.SCL
