# Fritzing sketch bme280 (saved by Fritzing 0.9.3b)

parts:
  Part1 = Intel Edison Arduinobreakout  # not connected
  Part2 = Base Shield V2
  Part3 = BME280 Breakout

nets:
  N1: Part2.pin_136, Part3.GND
  N2: Part2.pin_137, Part3.3.3V
  N3: Part2.pin_138, Part3.SDI/SDA
  N4: Part2.pin_139, Part3.SCK/SCL
