# Fritzing sketch grovebutton (saved by Fritzing 0.9.3b)

parts:
  Part1 = Intel Edison Arduinobreakout  # not connected
  Part2 = Base Shield V2
  Grove1 = Grove Button

nets:
  N1: Part2.pin_92, Grove1.GND
  N2: Part2.pin_93, Grove1.VCC
  N3: Part2.pin_94, Grove1.NC
  N4: Part2.pin_95, Grove1.SIG
