# Fritzing sketch grovebuzzer (saved by Fritzing 0.9.3b)

parts:
  Part1 = Intel Edison Arduinobreakout  # not connected
  Part2 = Base Shield V2
  Grove2 = Grove Buzz

nets:
  N1: Part2.pin_92, Grove2.GND
  N2: Part2.pin_93, Grove2.VCC
  N3: Part2.pin_95, Grove2.SIG
