# Fritzing sketch groveled (saved by Fritzing 0.9.3b)

parts:
  Part1 = Intel Edison Arduinobreakout  # not connected
  Part2 = Base Shield V2
  Grove_LED_Red1 = Grove LED Red

nets:
  N1: Part2.pin_92, Grove_LED_Red1.GND
  N2: Part2.pin_93, Grove_LED_Red1.NC2
  N3: Part2.pin_94, Grove_LED_Red1.NC1
  N4: Part2.pin_95, Grove_LED_Red1.SIG

custom parts:
  Grove LED Red: LED red, Grove connector.
