# Fritzing sketch groverelay (saved by Fritzing 0.9.3b)

parts:
  Part1 = Intel Edison Arduinobreakout  # not connected
  Part2 = Base Shield V2
  Grove_Relay1 = Grove Relay

nets:
  N1: Part2.pin_92, Grove_Relay1.GND
  N2: Part2.pin_93, Grove_Relay1.VCC
  N3: Part2.pin_94, Grove_Relay1.NC
  N4: Part2.pin_95, Grove_Relay1.SIG

custom parts:
  Grove Relay: Relay, Grove connector.
