# Fritzing sketch grovetouch (saved by Fritzing 0.9.3b)

parts:
  Part1 = Intel Edison Arduinobreakout  # not connected
  Part2 = Base Shield V2
  Grove_Touch_Sensor(P)2 = Grove Touch Sensor (P)

nets:
  N1: Part2.pin_92, Grove_Touch_Sensor(P)2.GND
  N2: Part2.pin_93, Grove_Touch_Sensor(P)2.VCC
  N3: Part2.pin_94, Grove_Touch_Sensor(P)2.NC
  N4: Part2.pin_95, Grove_Touch_Sensor(P)2.SIG

custom parts:
  Grove Touch Sensor (P): Touch sensor, Grove connector, panel mount.
