# Fritzing sketch jhd1313m1 (saved by Fritzing 0.9.3b)

parts:
  Part1 = Intel Edison Arduinobreakout  # not connected
  Part2 = Base Shield V2
  Grove3 = Grove OLED 128x96

nets:
  N1: Part2.pin_124, Grove3.GND
  N2: Part2.pin_125, Grove3.VCC
  N3: Part2.pin_126, Grove3.SDA
  N4: Part2.pin_127, Grove3.SCL
