# Fritzing sketch mma7660 (saved by Fritzing 0.9.3b)

parts:
  Part1 = Intel Edison Arduinobreakout  # not connected
  Part2 = Base Shield V2
  Grove1 = Grove 3 Axis Digital Accelerometer 16g

nets:
  N1: Part2.pin_136, Grove1.GND
  N2: Part2.pin_137, Grove1.VCC
  N3: Part2.pin_138, Grove1.SDA
  N4: Part2.pin_139, Grove1.SCL
