# Fritzing sketch tmp006 (saved by Fritzing 0.9.3b)

parts:
  Part1 = Intel Edison Arduinobreakout  # not connected
  Part2 = Base Shield V2
  Part4 = TMP006 Thermopile Sensor

nets:
  N1: Part2.pin_136, Part4.GND
  N2: Part2.pin_137, Part4.VCC
  N3: Part2.pin_138, Part4.SDA
  N4: Part2.pin_139, Part4.SCL

custom parts:
  TMP006 Thermopile Sensor: Unlike all the other temperature sensors we have, this breakout has a really cool IR sensor from TI that can measure the temperature of an object without touching it! Simply point the sensor towards what you want to measure and it will detect the temperature by absorbing IR waves emitted. The embedded thermopile sensor generates a very very small voltage depending on how much IR there is, and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
